# Fritzing sketch sketch_2 (saved by Fritzing 0.9.3b)

parts:
  Componente1 = Arduino Nano (Rev3.0) (ICSP)
  U1 = mystery part, 15 pins [chip_label=?]
  U2 = mystery part, 15 pins [chip_label=?]
  MUX1 = 74HC4051 [package="DIP (Dual Inline) [THT]"]
  SS49E_1 = Mystery Part - 3 pins [chip_label=SS49E package=THT]
  SS49E_2 = Mystery Part - 3 pins [chip_label=SS49E package=THT]
  SS49E_3 = Mystery Part - 3 pins [chip_label=SS49E package=THT]
  SS49E_4 = Mystery Part - 3 pins [chip_label=SS49E package=THT]
  SS49E_5 = Mystery Part - 3 pins [chip_label=SS49E package=THT]
  SS49E_6 = Mystery Part - 3 pins [chip_label=SS49E package=THT]
  SS49E_7 = Mystery Part - 3 pins [chip_label=SS49E package=THT]
  SS49E_8 = Mystery Part - 3 pins [chip_label=SS49E package=THT]

nets:
  N1: Componente1.D1/TX, U2.pin15
  N2: Componente1.D0/RX, U2.pin14
  N3: Componente1.RESET, U1.pin3, U2.pin13
  N4: Componente1.GND, U1.pin2, U2.pin12
  N5: Componente1.D2, U2.pin11
  N6: Componente1.D3, U2.pin10
  N7: Componente1.D4, U2.pin9
  N8: Componente1.D5, U2.pin8
  N9: Componente1.D6, U2.pin7
  N10: Componente1.D7, U2.pin6
  N11: Componente1.D8, U2.pin5
  N12: Componente1.D9, U2.pin4
  N13: Componente1.D10, U2.pin3
  N14: Componente1.D11/MOSI, U2.pin2
  N15: Componente1.D12/MISO, U2.pin1
  N16: Componente1.VIN, U1.pin1
  N17: Componente1.5V, U1.pin4
  N18: Componente1.A7, U1.pin5
  N19: Componente1.A6, U1.pin6
  N20: Componente1.A5, U1.pin7
  N21: Componente1.A4, U1.pin8
  N22: Componente1.A3, U1.pin9
  N23: Componente1.A2, U1.pin10
  N24: Componente1.A1, U1.pin11
  N25: Componente1.A0, U1.pin12
  N26: Componente1.AREF, U1.pin13
  N27: Componente1.3V3, U1.pin14
  N28: Componente1.D13/SCK, U1.pin15
  N29: MUX1.IO4, SS49E_5.Output
  N30: MUX1.IO6, SS49E_7.Output
  N31: MUX1.IO7, SS49E_8.Output
  N32: MUX1.IO5, SS49E_6.Output
  N33: MUX1.VEE, MUX1.VSS, SS49E_1.Ground, SS49E_2.Ground, SS49E_3.Ground, SS49E_4.Ground, SS49E_5.Ground, SS49E_6.Ground, SS49E_7.Ground, SS49E_8.Ground
  N34: MUX1.IO3, SS49E_4.Output
  N35: MUX1.IO0, SS49E_1.Output
  N36: MUX1.IO1, SS49E_2.Output
  N37: MUX1.IO2, SS49E_3.Output
  VCC: MUX1.VDD, SS49E_1.Vcc, SS49E_2.Vcc, SS49E_3.Vcc, SS49E_4.Vcc, SS49E_5.Vcc, SS49E_6.Vcc, SS49E_7.Vcc, SS49E_8.Vcc

custom parts:
  74HC4051: 8 channel analog multiplexer/demultiplexer
  Mystery Part - 3 pins: A dummy, proxy, ersatz, stand-in part for whatever you want. With 3 pins on a 100 mil inline pin header footprint.
